# Fritzing sketch BoxDomotic (saved by Fritzing 0.8.7b)
circuit board: 8.46667cm x 5.64444cm
perfboards: 1

parts:
  Parte1 = Arduino Nano (Rev3.0)
  R1 = Photocell (LDR) [package=THT]
  DS1 = DS18B20 1-Wire Temperature Sensor Probe
  Sensore_PIR_HC-SR502 = HC-SR501 Body Sensor Module
  U1 = 4-Channel 5v Relay Shield [package=relay-4ch5v10a]  # not connected
  U2 = 2-Channel 5v Relay Shield [package=relay-2ch5v10a]  # not connected
  Parte2 = NRF24L01
  R2 = Resistor [tolerance=±5% resistance=220 package=THT]
  R3 = Resistor [tolerance=±5% resistance=220 package=THT]
  R4 = Resistor [tolerance=±5% resistance=220 package=THT]
  R5 = Resistor [tolerance=±5% resistance=220 package=THT]
  R6 = Photocell (LDR) [package=THT]
  DS2 = DS18B20 1-Wire Temperature Sensor Probe
  Parte4 = Arduino Nano (Rev3.0)
  J1 = male pin header, 12 pins [form="♂ (male)"]
  J2 = male pin header, 10 pins [form="♂ (male)"]
  J3 = male pin header, 4 pins [form="♂ (male)"]  # not connected
  J4 = male pin header, 4 pins [form="♂ (male)"]  # not connected
  J5 = male pin header, 6 pins [form="♂ (male)"]
  J6 = male pin header, 4 pins [form="♂ (male)"]
  J7 = male pin header, 4 pins [form="♂ (male)"]

nets:
  GND: Parte1.GND, DS1.GND, Sensore_PIR_HC-SR502.GND, Parte2.GND, R3.Pin_1
  N1: Parte1.D2, DS1.DQ, R2.Pin_0
  N2: Parte1.D3, Sensore_PIR_HC-SR502.OUT
  N3: Parte1.D9, Parte2.CE
  N4: Parte1.D10, Parte2.CSN
  N5: Parte1.D11/MOSI, Parte2.MOSI
  N6: Parte1.D12/MISO, Parte2.MISO
  5V: Parte1.5V, R1.pin_1, DS1.VDD, Sensore_PIR_HC-SR502.VCC, R2.Pin_1
  N7: Parte1.A7, R1.pin_0, R3.Pin_0
  3V3: Parte1.3V3, Parte2.VCC
  N8: Parte1.D13/SCK, Parte2.SCK
  N9: R4.Pin_0, R6.pin_0, DS2.VDD, J7.pin4
  N10: R5.Pin_1, R6.pin_1, Parte4.A7, J5.pin2
  GND_2: DS2.GND, Parte4.GND, J5.pin5, J7.pin2
  N11: DS2.DQ, Parte4.D2
  N12: Parte4.RESET, J5.pin4
  N13: Parte4.D3, J1.pin10, J7.pin3
  N14: Parte4.D9, J1.pin4
  N15: Parte4.D10, J1.pin3
  N16: Parte4.D11/MOSI, J1.pin2
  N17: Parte4.D12/MISO, J1.pin1
  N18: Parte4.VIN, J5.pin6
  N19: Parte4.5V, J5.pin3
  N20: Parte4.A6, J2.pin6, J5.pin1
  N21: Parte4.AREF, J6.pin4
  N22: Parte4.3V3, J6.pin3
  N23: Parte4.D13/SCK, J6.pin2
  N24: J1.pin5, J2.pin1
  N25: J1.pin6, J2.pin2
  N26: J1.pin7, J2.pin3
  N27: J1.pin8, J2.pin4
  N28: J1.pin9, J2.pin5

notes:
  GND&VCC
  from PowerSupply

custom parts:
  HC-SR501 Body Sensor Module: Pyroelectric Infrared PIR Motion Sensor Detector Module
  4-Channel 5v Relay Shield: 4 Channel 5v Relay Shield w. 2x SPD-06VDC-SD-C
  2-Channel 5v Relay Shield: 2 Channel 5v Relay Shield w. 2x SPD-06VDC-SD-C
